// Logisim project SAP1_versao5_claudio.circ as structural Verilog: 16 circuits, main circuit main
module main (
  input  Reset,
  output [3:0] Dados,
  output [3:0] \Dados___Endereços ,
  output out_4,
  output out_5,
  output out_6,
  output out_7,
  output out_8,
  output out_9,
  output out_10,
  output out_11
);

  wire CLK, Clock_out, controlador_sequencializador_rom_1_hlt, Cp, Ea, Ei, Ep, Eu, IncDec, Li, Lp, Mul, nCE,
       nEi, nLa, nLb, nLi, nLm, nLo, not_1_out, not_2_out, not_3_out, not_4_out, RDnWR,
       \registrador_instruções_1_i4 , \registrador_instruções_1_i5 , \registrador_instruções_1_i6 ,
       \registrador_instruções_1_i7 , Su;
  wire [3:0] rem_1_remout, \Timer_saída , Unidade_de_comunicacao_ligar_display1,
       Unidade_de_comunicacao_ligar_display2;
  wire [7:0] acumulador_1_a_out_ula, registrador_b_1_b_dataout;

  Hex_Digit_Display hex_digit_display_1 (.value(Unidade_de_comunicacao_ligar_display1));  // open: dp
  Unidade_de_comunicacao Unidade_de_comunicacao (
    .rx_barramento1(Dados), .rx_barramento2(\Dados___Endereços ),
    .ligar_display1(Unidade_de_comunicacao_ligar_display1),
    .ligar_display2(Unidade_de_comunicacao_ligar_display2));  // open: in_1, Tx_barramento1, Tx_barramento2, ERX, CLK, CLR, LTX, Erxout
  Hex_Digit_Display hex_digit_display_2 (.value(Unidade_de_comunicacao_ligar_display2));  // open: dp
  Clock Clock (.out(Clock_out));
  not not_1 (not_1_out, CLK);
  not not_2 (not_2_out, Reset);
  not not_3 (not_3_out, nCE);
  assign CLK = not_4_out ? Clock_out : 1'bz;  // Controlled_Buffer controlled_buffer_1
  not not_4 (not_4_out, controlador_sequencializador_rom_1_hlt);
  REM rem_1 (.in_1(\Dados___Endereços ), .nLm(nLm), .CLK(CLK), .REMOut(rem_1_remout));
  Contador_Programa contador_programa_1 (
    .Cp(Cp), .nCLK(not_1_out), .nCLR(not_2_out), .Ep(Ep), .Cp_Out(\Dados___Endereços ), .Lp(Lp),
    .Cp_In(\Dados___Endereços ));
  \Memória_RAM  \memória_ram_1  (
    .in_2(rem_1_remout), .nCE(not_3_out), .CLK(CLK), .out_6({Dados, \Dados___Endereços }), .RD_nWR(RDnWR),
    .in_1({Dados, \Dados___Endereços }));
  \Registrador_Instruções  \registrador_instruções_1  (
    .in_1({Dados, \Dados___Endereços }), .nLi(nLi), .CLK(CLK), .CLR(Reset), .nEi(nEi),
    .out_6(\Dados___Endereços ), .I4(\registrador_instruções_1_i4 ), .I5(\registrador_instruções_1_i5 ),
    .I6(\registrador_instruções_1_i6 ), .I7(\registrador_instruções_1_i7 ));
  Controlador_Sequencializador_ROM controlador_sequencializador_rom_1 (
    .CLK(CLK), .CLR(Reset), .HLT(controlador_sequencializador_rom_1_hlt), .Cp(Cp), .Ep(Ep), .nLm(nLm),
    .nCE(nCE), .nLl(nLi), .nEl(nEi), .nLa(nLa), .Ea(Ea), .Su(Su), .Eu(Eu), .nLb(nLb), .nLo(nLo),
    .I7(\registrador_instruções_1_i7 ), .I6(\registrador_instruções_1_i6 ),
    .I4(\registrador_instruções_1_i4 ), .IncDec(IncDec), .RDnWR(RDnWR), .Mul(Mul), .Lp(Lp),
    .I5(\registrador_instruções_1_i5 ));
  Acumulador acumulador_1 (
    .A_In({Dados, \Dados___Endereços }), .nLa(nLa), .CLK(CLK), .Ea(Ea), .A_Out_ULA(acumulador_1_a_out_ula),
    .A_Out({Dados, \Dados___Endereços }));
  Somador_Subtrator somador_subtrator_1 (
    .Su(Su), .B_data(registrador_b_1_b_dataout), .A_dataOut2({Dados, \Dados___Endereços }),
    .A_data(acumulador_1_a_out_ula), .Eu(Eu), .IncDec(IncDec), .mul(Mul));
  Registrador_B registrador_b_1 (
    .B_dataIn({Dados, \Dados___Endereços }), .B_dataOut(registrador_b_1_b_dataout), .nLb(nLb), .CLK(CLK));
  Entrada_8_bits entrada_8_bits_1 (
    .Ei(Ei), .CLK(CLK), .CLR(Reset), .Li(Li), .E_barramento1(Dados), .E_barramento2(\Dados___Endereços ));  // open: in_3
  Hex_Digit_Display hex_digit_display_3 (.value({out_4, out_5, out_6, out_7}));  // open: dp
  \Indicação_Visual  \indicação_visual_1  (
    .Input({Dados, \Dados___Endereços }),
    .Output({out_4, out_5, out_6, out_7, out_8, out_9, out_10, out_11}), .nLo(nLo), .CLK(CLK), .CLR(Reset));
  Hex_Digit_Display hex_digit_display_4 (.value(\Timer_saída ));  // open: dp
  Timer Timer (.\Saída (\Timer_saída ), .CLK(CLK), .CLR(Reset));
  Hex_Digit_Display hex_digit_display_5 (.value({out_8, out_9, out_10, out_11}));  // open: dp
  DotMatrix #(.matrixcols(8), .matrixrows(1), .dotshape("circle")) dotmatrix_1 (
    .col0(out_4), .col1(out_5), .col2(out_6), .col3(out_7), .col4(out_8), .col5(out_9), .col6(out_10),
    .col7(out_11));

  // Other names for the same wires on the sheet: CLR = Reset

  // Notes on the sheet:
  //   SAP-1 EM LOGISIM Modificado Cláudio - Versão 5 2024
  //   Arquitetura de Computadores I
  //   Timer
  //   Conta de 1 até 6, representando os tempos de clock T1 a T6
  //   Grupo:
  //   Instruções:
  //   LDA 0000: A<-*(MEM)
  //   ADD 0001: A<-A+B
  //   SUB 0010: A<-A-B
  //   INC 0011: A<=A+1
  //   DEC 0100: A<=A-1
  //   MUL 0101: A<-AxB
  //   JMP 0110: CP<-endereço de salto
  //   OUT 1110: exibir o valor
  //   HLT 1111: interromper o circuito
  //   Como usar:
  //   Adicione as operações no bloco de memória RAM,
  //   execute um RESET e envie pulsos de clock.
  //   Professor,
  //   Matheus Mota Cavalcante
  //   Tentei de algumas formas mas não consegui configurar os sinais corretamente na ROM
  //   Provavelmente está dando conflito no envio de dados ao barramento e por isso o circuito dá erro
endmodule

module Contador_Programa (
  input  Lp,
  input  [3:0] Cp_In,
  input  Cp,
  input  nCLK,
  input  nCLR,
  input  Ep,
  output [3:0] Cp_Out
);

  wire not_1_out;
  wire [3:0] counter_1_q;

  not not_1 (not_1_out, nCLR);
  Counter #(.width(4), .max('hf), .trigger("falling")) counter_1 (
    .load(Lp), .D(Cp_In), .count(Cp), .Q(counter_1_q), .clk(nCLK), .clr(not_1_out));  // open: carry
  assign Cp_Out = Ep ? counter_1_q : 4'bz;  // Controlled_Buffer controlled_buffer_1
endmodule

module REM (
  input  [3:0] in_1,
  input  nLm,
  input  CLK,
  output [3:0] REMOut
);

  wire not_1_out;

  not not_1 (not_1_out, nLm);
  Register #(.width(4)) register_1 (.D(in_1), .en(not_1_out), .Q(REMOut), .clk(CLK));  // open: clr
endmodule

module \Memória_RAM  (
  input  [7:0] in_1,
  input  [3:0] in_2,
  input  nCE,
  input  CLK,
  input  RD_nWR,
  output [7:0] out_6
);

  wire not_1_out;
  wire [7:0] controlled_buffer_1_out;

  assign controlled_buffer_1_out = not_1_out ? in_1 : 8'bz;  // Controlled_Buffer controlled_buffer_1
  RAM #(.addrWidth(4)) ram_1 (
    .addr(in_2), .data(controlled_buffer_1_out), .sel(nCE), .clk(CLK), .ld(RD_nWR), .clr(1'b0));
  assign out_6 = RD_nWR ? controlled_buffer_1_out : 8'bz;  // Controlled_Buffer controlled_buffer_2
  not not_1 (not_1_out, RD_nWR);

  // Notes on the sheet:
  //   Programas Exemplo
  //   Exemplo 1:  02 + 03 - 04 + 02 = 03
  //   0f e0 1e e0 2d e0 1f e0 f0 00 00 00 00 04 03 02
  //   Exemplo 2:  150 + 70 - 50 + 100 = ? 270
  //   0f e0 1e e0 2d e0 1c e0 f0 00 00 00 64 32 46 96
  //   Exemplo 3:  5 x 2 - 1 - 2 + 1 = 8
  //   0f e0 5e e0 40 e0 2e e0 30 e0 f0 00 00 00 02 05
  //   Exemplo 4:  Carrega A=1,Exibe A, Inc A, Exibe A, JMP para Inc A 
  //   0f e0 30 e0 62 f0
  //   Exemplo 5:  Contador Progressivo 
  //   Exemplo 6:  Gera a Série de Fibonacci 
  //    Click com o botão direito do mouse sobre a RAM e carregue alguma programação disponivel
endmodule

module \Registrador_Instruções  (
  input  [7:0] in_1,
  input  nLi,
  input  CLK,
  input  CLR,
  input  nEi,
  output [3:0] out_6,
  output I4,
  output I5,
  output I6,
  output I7
);

  wire not_1_out, not_2_out;
  wire [3:0] register_1_q;

  not not_1 (not_1_out, nLi);
  not not_2 (not_2_out, nEi);
  Register register_1 (.D(in_1), .en(not_1_out), .Q({I7, I6, I5, I4, register_1_q}), .clk(CLK), .clr(CLR));
  assign out_6 = not_2_out ? register_1_q : 4'bz;  // Controlled_Buffer controlled_buffer_1
endmodule

module Acumulador (
  input  [7:0] A_In,
  input  nLa,
  input  CLK,
  input  Ea,
  output [7:0] A_Out_ULA,
  output [7:0] A_Out
);

  wire not_1_out;

  not not_1 (not_1_out, nLa);
  Register register_1 (.D(A_In), .en(not_1_out), .Q(A_Out_ULA), .clk(CLK));  // open: clr
  assign A_Out = Ea ? A_Out_ULA : 8'bz;  // Controlled_Buffer controlled_buffer_1
endmodule

module Somador_Subtrator (
  input  Su,
  input  IncDec,
  input  [7:0] B_data,
  input  [7:0] A_data,
  input  Eu,
  input  mul,
  output [7:0] A_dataOut2
);

  wire not_1_out;
  wire [7:0] adder_1_out, controlled_buffer_1_out, multiplier_1_out, xor_1_out;

  not not_1 (not_1_out, IncDec);
  assign controlled_buffer_1_out = IncDec ? 8'h1 : 8'bz;  // Controlled_Buffer controlled_buffer_1
  assign controlled_buffer_1_out = not_1_out ? B_data : 8'bz;  // Controlled_Buffer controlled_buffer_2
  assign xor_1_out = {8{Su}} ^ controlled_buffer_1_out;  // XOR_Gate xor_1, 8 bits wide
  Adder adder_1 (.a(xor_1_out), .b(A_data), .out(adder_1_out), .cin(Su));  // open: cout
  Multiplier multiplier_1 (.a(B_data), .b(A_data), .out(multiplier_1_out));  // open: cin, cout
  assign A_dataOut2 = Eu ? adder_1_out : 8'bz;  // Controlled_Buffer controlled_buffer_3
  assign A_dataOut2 = mul ? multiplier_1_out : 8'bz;  // Controlled_Buffer controlled_buffer_4
endmodule

module Registrador_B (
  input  [7:0] B_dataIn,
  input  nLb,
  input  CLK,
  output [7:0] B_dataOut
);

  wire not_1_out;

  Register register_1 (.D(B_dataIn), .en(not_1_out), .Q(B_dataOut), .clk(CLK));  // open: clr
  not not_1 (not_1_out, nLb);
endmodule

module Decodificador (
  input  l7,
  input  l6,
  input  l5,
  input  l4,
  output LDA,
  output ADD,
  output SUB,
  output OUT,
  output HLT
);

  wire and_1_out, and_2_out, and_3_out, and_4_out, and_5_out, not_1_out, not_2_out, not_3_out, not_4_out;

  not not_1 (not_1_out, l7);
  not not_2 (not_2_out, l6);
  not not_3 (not_3_out, l5);
  not not_4 (not_4_out, l4);
  and and_1 (and_1_out, not_1_out, not_2_out, not_3_out, not_4_out);
  buf buffer_1 (LDA, and_1_out);
  buf buffer_2 (ADD, and_2_out);
  and and_2 (and_2_out, not_1_out, not_2_out, not_3_out, l4);
  buf buffer_3 (SUB, and_3_out);
  and and_3 (and_3_out, not_1_out, not_2_out, l5, not_4_out);
  buf buffer_4 (OUT, and_4_out);
  and and_4 (and_4_out, l7, l6, l5, not_4_out);
  and and_5 (and_5_out, l7, l6, l5, l4);
  buf buffer_5 (HLT, and_5_out);
endmodule

module \Indicação_Visual  (
  input  [7:0] Input,
  input  nLo,
  input  CLK,
  input  CLR,
  output [7:0] Output
);

  wire not_1_out;

  not not_1 (not_1_out, nLo);
  Register register_1 (.D(Input), .en(not_1_out), .Q(Output), .clk(CLK), .clr(CLR));
endmodule

module Controlador_Sequencializador_ROM (
  input  I7,
  input  I6,
  input  I5,
  input  I4,
  input  CLK,
  input  CLR,
  output Cp,
  output Ep,
  output nLm,
  output nCE,
  output nLl,
  output nEl,
  output nLa,
  output Ea,
  output Su,
  output Eu,
  output nLb,
  output nLo,
  output IncDec,
  output RDnWR,
  output Mul,
  output Lp,
  output HLT
);

  wire and_2_out, and_3_out, and_5_out, and_6_out, clr_t, load, nop, nor_1_out, not_1_out, not_2_out,
       or_1_out, shift_register_1_q0, shift_register_1_q1, shift_register_1_q3, shift_register_1_q4;
  wire [4:0] counter_1_q, rom_1_data;

  and and_1 (HLT, I7, I6, I5, I4);
  ROM #(.addrWidth(4), .dataWidth(5)) rom_1 (.addr({I7, I6, I5, I4}), .data(rom_1_data));  // open: sel
  or or_1 (or_1_out, CLR, nop);
  or or_2 (clr_t, or_1_out, nor_1_out);
  not not_1 (not_1_out, load);
  not not_2 (not_2_out, CLK);
  Shift_Register #(.length(6)) shift_register_1 (
    .in(nor_1_out), .clk(CLK), .clr(or_1_out), .q0(shift_register_1_q0), .q1(shift_register_1_q1), .q2(load),
    .q3(shift_register_1_q3), .q4(shift_register_1_q4));  // open: shift, out, load, d0, d1, d2, d3, d4, d5, q5
  Counter #(.width(5), .max('h1f), .ongoal("continue")) counter_1 (
    .load(load), .D(rom_1_data), .count(not_1_out), .Q(counter_1_q), .clk(not_2_out), .clr(clr_t));  // open: carry
  nor nor_1 (nor_1_out, shift_register_1_q0, shift_register_1_q1, load, shift_register_1_q3, shift_register_1_q4);
  ROM #(.addrWidth(5), .dataWidth(16)) rom_2 (
    .addr(counter_1_q), .data({Cp, Ep, nLm, nCE, nLl, nEl, nLa, Ea, Su, Eu, nLb, nLo, IncDec, RDnWR, Mul, Lp}));  // open: sel
  and and_2 (and_2_out, ~Cp, ~Ep, nLm, nCE);  // AND_Gate
  and and_3 (and_3_out, nLl, nEl, nLa, ~Ea);  // AND_Gate
  and and_4 (nop, and_2_out, and_3_out, and_5_out, and_6_out);
  and and_5 (and_5_out, ~Su, ~Eu, nLb, nLo);  // AND_Gate
  and and_6 (and_6_out, ~IncDec, ~RDnWR, ~Mul, ~Lp);  // AND_Gate

  // Notes on the sheet:
  //   contents of rom_1 (hex, n*v repeats v):
  //   3 6 9 10 13 16 19 1c 6*0 c
  //   contents of rom_2 (hex, n*v repeats v):
  //   5e30 be30 2634 1a30 2c34 3e30 1a30 2e14 3c70 1a30 2e14 3cf0 3f20 3e30 3e30 0 3c78 3e30 3e30 3cf8
  //   3e30 3e30 1a30 2e14 3c32 3a31 3e30 3e30 1a30 2f30 3e30
endmodule

module Cont_Prog (
  input  EO,
  input  CLK,
  input  CLK_EN,
  input  LOAD,
  input  D0,
  input  D1,
  input  D2,
  input  D3,
  input  CLEAR,
  output Q0,
  output Q1,
  output Q2,
  output Q3
);

  wire and_1_out, and_2_out, and_3_out, and_4_out, and_5_out, and_6_out, and_7_out, and_8_out, and_9_out,
       and_10_out, ff_t_1_q, ff_t_2_q, ff_t_3_q, ff_t_4_q, not_1_out, not_2_out, not_3_out, not_4_out;

  and and_1 (and_1_out, LOAD, D0);
  assign Q0 = EO ? ff_t_1_q : 1'bz;  // Controlled_Buffer controlled_buffer_1
  FF_T ff_t_1 (
    .T(1'b1), .CLK(CLK), .EN(CLK_EN), .Q(ff_t_1_q), .sPRE(and_1_out), .PRE(1'b0), .sCLR(and_2_out),
    .CLR(CLEAR));  // open: nQ
  and and_2 (and_2_out, LOAD, not_1_out);
  not not_1 (not_1_out, D0);
  and and_3 (and_3_out, LOAD, D1);
  FF_T ff_t_2 (
    .T(ff_t_1_q), .CLK(CLK), .EN(CLK_EN), .Q(ff_t_2_q), .sPRE(and_3_out), .PRE(1'b0), .sCLR(and_4_out),
    .CLR(CLEAR));  // open: nQ
  and and_4 (and_4_out, LOAD, not_2_out);
  not not_2 (not_2_out, D1);
  assign Q1 = EO ? ff_t_2_q : 1'bz;  // Controlled_Buffer controlled_buffer_2
  and and_5 (and_5_out, LOAD, D2);
  and and_6 (and_6_out, ff_t_1_q, ff_t_2_q);
  and and_7 (and_7_out, LOAD, not_3_out);
  not not_3 (not_3_out, D2);
  assign Q2 = EO ? ff_t_3_q : 1'bz;  // Controlled_Buffer controlled_buffer_3
  FF_T ff_t_3 (
    .T(and_6_out), .CLK(CLK), .EN(CLK_EN), .Q(ff_t_3_q), .sPRE(and_5_out), .PRE(1'b0), .sCLR(and_7_out),
    .CLR(CLEAR));  // open: nQ
  and and_8 (and_8_out, LOAD, D3);
  and and_9 (and_9_out, and_6_out, ff_t_3_q);
  and and_10 (and_10_out, LOAD, not_4_out);
  not not_4 (not_4_out, D3);
  assign Q3 = EO ? ff_t_4_q : 1'bz;  // Controlled_Buffer controlled_buffer_4
  FF_T ff_t_4 (
    .T(and_9_out), .CLK(CLK), .EN(CLK_EN), .Q(ff_t_4_q), .sPRE(and_8_out), .PRE(1'b0), .sCLR(and_10_out),
    .CLR(CLEAR));  // open: nQ
endmodule

module FF_T (
  input  sPRE,
  input  PRE,
  input  T,
  input  CLK,
  input  EN,
  input  sCLR,
  input  CLR,
  output Q,
  output nQ
);

  wire and_1_out, and_2_out, not_1_out, not_2_out, or_1_out, or_2_out;

  or or_1 (or_1_out, sPRE, T);
  not not_1 (not_1_out, sPRE);
  and and_1 (and_1_out, not_1_out, T);
  and and_2 (and_2_out, or_1_out, not_2_out);
  not not_2 (not_2_out, sCLR);
  or or_2 (or_2_out, and_1_out, sCLR);
  J_K_Flip_Flop j_k_ff_1 (.J(and_2_out), .clk(CLK), .K(or_2_out), .Q(Q), .Qn(nQ), .preset(PRE), .en(EN), .reset(CLR));
endmodule

module Timer (
  input  CLK,
  input  CLR,
  output [3:0] \Saída 
);

  wire [2:0] Timer_q;

  Counter #(.width(3), .max('h5)) Timer (.Q(Timer_q), .clk(CLK), .clr(CLR));  // open: load, D, count, carry
  Adder #(.width(3)) adder_1 (.a(Timer_q), .b(3'b001), .out(\Saída [2:0]));  // open: cin, cout

  assign \Saída [3] = 1'b0;
endmodule

module Entrada_8_bits (
  input  Li,
  input  Ei,
  input  [7:0] in_3,
  input  CLK,
  input  CLR,
  output [3:0] E_barramento1,
  output [3:0] E_barramento2
);

  wire undriven;
  wire [7:0] register_1_q;

  assign {E_barramento2, E_barramento1} = undriven ? register_1_q : 8'bz;  // Controlled_Buffer controlled_buffer_1
  Register register_1 (.D(in_3), .en(Li), .Q(register_1_q), .clk(CLK), .clr(CLR));
endmodule

module Unidade_de_comunicacao (
  input  [7:0] in_1,
  input  ERX,
  input  CLK,
  input  CLR,
  input  Erxout,
  input  [3:0] Tx_barramento1,
  input  [3:0] Tx_barramento2,
  input  LTX,
  output [3:0] rx_barramento1,
  output [3:0] rx_barramento2,
  output [3:0] ligar_display1,
  output [3:0] ligar_display2
);

  wire [7:0] register_1_q;

  Register register_1 (.D(in_1), .en(ERX), .Q(register_1_q), .clk(CLK), .clr(CLR));
  assign {rx_barramento2, rx_barramento1} = Erxout ? register_1_q : 8'bz;  // Controlled_Buffer controlled_buffer_1
  Register register_2 (
    .D({Tx_barramento2, Tx_barramento1}), .en(LTX), .Q({ligar_display2, ligar_display1}), .clk(CLK), .clr(CLR));

  // Notes on the sheet:
  //   TX
  //   Rx
endmodule
